# Fritzing sketch insolation_sensor (saved by Fritzing 0.9.3b)
breadboards: 1

parts:
  WeMos_D1_Mini1 = WeMos D1 Mini
  R1 = Photocell (LDR) [package=THT]
  R2 = Resistor [tolerance=±5% power=0.25 resistance=10k package=THT]

nets:
  N1: WeMos_D1_Mini1.3V3, R1.pin_1
  N2: WeMos_D1_Mini1.A0, R1.pin_0, R2.Pin_0
  N3: WeMos_D1_Mini1.G, R2.Pin_1
